// Logisim project root.circ as structural Verilog
module main (
);

  wire button_1_out, button_2_out, clk, controlpath_1_load, controlpath_1_store;
  wire [7:0] adder_1_out, controlpath_1_sign, datapath_1_address, datapath_1_dataout, ram_1_dout,
       register_1_q;
  wire [23:0] rom_1_data;

  Clock clock_1 (.out(clk));
  Register register_1 (.D(adder_1_out), .Q(register_1_q), .clk(clk), .clr(button_1_out));  // open: en
  Button button_1 (.out(button_1_out));
  Adder adder_1 (.a(register_1_q), .b(8'h1), .out(adder_1_out));  // open: cin, cout
  ROM #(.dataWidth(24)) rom_1 (.addr(register_1_q), .data(rom_1_data));
  DataPath datapath_1 (
    .Sign(controlpath_1_sign), .DataIn(ram_1_dout), .Params(rom_1_data[15:0]), .clk(clk),
    .Address(datapath_1_address), .DataOut(datapath_1_dataout));
  ControlPath controlpath_1 (
    .Opcode(rom_1_data[23:16]), .Load(controlpath_1_load), .Store(controlpath_1_store),
    .Sign(controlpath_1_sign));
  RAM #(.clearpin("true"), .\type ("nonvolatile")) ram_1 (
    .addr(datapath_1_address), .we(controlpath_1_store), .oe(controlpath_1_load), .clk(clk),
    .din(datapath_1_dataout), .dout(ram_1_dout), .clr(button_2_out));
  Button button_2 (.out(button_2_out));

  // Notes on the sheet:
  //   contents of rom_1 (hex, n*v repeats v):
  //   440003 410000 420100 830100 410101 420201 930200
endmodule

module ControlPath (
  input  [7:0] Opcode,
  output Load,
  output Store,
  output [7:0] Sign
);


  assign Load = 1'b1;
  assign Sign = {4'b1111, Opcode[2], 3'b010};
  assign Store = Opcode[2];
endmodule

module DataPath (
  input  [7:0] Sign,
  input  [7:0] DataIn,
  input  [15:0] Params,
  input  clk,
  output [7:0] Address,
  output [7:0] DataOut
);

  wire decoder_1_out0, decoder_1_out1;
  wire [4:0] multiplexer_4_out;
  wire [7:0] multiplexer_1_out, multiplexer_2_out;

  Multiplexer #(.width(8)) multiplexer_1 (.in0(DataIn), .in1(Params[7:0]), .out(multiplexer_1_out), .sel(Sign[2]));
  Multiplexer #(.width(8)) multiplexer_2 (.in0(DataIn), .in1(Params[7:0]), .out(multiplexer_2_out), .sel(Sign[1]));
  ULA ula_1 ();
  Multiplexer #(.width(8)) multiplexer_3 (.in0(multiplexer_2_out), .out(DataOut), .sel(Sign[0]));  // open: in1
  Multiplexer #(.width(5)) multiplexer_4 (.in0(Params[12:8]), .in1({5{1'b1}}), .out(multiplexer_4_out), .sel(Sign[3]));
  Decoder #(.enable("false"), .select(5)) decoder_1 (
    .out0(decoder_1_out0), .out1(decoder_1_out1), .sel(multiplexer_4_out));  // open: out2, out3, out4, out5, out6, out7, out8, out9, out10, out11, out12, out13, out14, out15, out16, out17, out18, out19, out20, out21, out22, out23, out24, out25, out26, out27, out28, out29, out30, out31
  Register regA (.D(multiplexer_1_out), .en(decoder_1_out0), .clk(clk));  // open: Q, clr
  Register regB (.D(multiplexer_1_out), .en(decoder_1_out1), .clk(clk));  // open: Q, clr

  assign Address = Params[15:8];
endmodule
